# Fritzing sketch BLDC (saved by Fritzing 0.9.2b)
breadboards: 1

parts:
  Part1 = Adafruit T-Cobbler Plus [part_number="Adafruit #1989 and #2028"]
  Part2 = HT SSOP28 pad [chip_label=PCA9685 package="HTSSOP28 pad"]
  M1 = ESC
  920KV_Motor1 = DJI 920 KV Motor  # not connected

nets:
  N1: Part1.SDA, Part2.27
  N2: Part1.SCL, Part2.26
  GND: Part1.GND, Part2.GND, Part2.2, Part2.3, Part2.4, Part2.5, Part2.24, Part2.25, M1.GND
  N3: Part1.+5V, Part2.28
  N4: Part2.6, M1.DATA

notes:
  3S (11.1V) DC LiPo Battery or some other source

custom parts:
  Adafruit T-Cobbler Plus: The Raspberry Pi has landed on the Maker World like a 40-GPIO pinned, quad-USB ported, credit card sized bomb of DIY joy. And while you can use most of our great Model B accessories by hooking up our downgrade cable, its probably a good time to upgrade your set up and accessorize using all of the 40 pins. That's why we now carry the Assembled Adafruit Pi T-Cobbler Plus - Breakout + Cable for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
  DJI 920 KV Motor: DJI Brushless Outrunner 2212/920K Motor F330-550
