# Fritzing sketch PCA9685-LED (saved by Fritzing 0.9.2b)
breadboards: 1

parts:
  Part1 = Adafruit T-Cobbler Plus [part_number="Adafruit #1989 and #2028"]
  Part2 = HT SSOP28 pad [chip_label=PCA9685 package="HTSSOP28 pad"]
  LED1 = smd LED [color="Red (633nm)" package="0603 [SMD]"]
  R1 = Resistor [tolerance=±5% resistance=220 package="0402 [SMD]"]

nets:
  N1: Part1.SDA, Part2.27
  N2: Part1.SCL, Part2.26
  GND: Part1.GND, Part2.GND, Part2.2, Part2.3, Part2.4, Part2.5, Part2.24, Part2.25, LED1.cathode
  N3: Part1.+5V, Part2.28
  N4: Part2.6, R1.Pin_0
  N5: LED1.anode, R1.Pin_1

custom parts:
  Adafruit T-Cobbler Plus: The Raspberry Pi has landed on the Maker World like a 40-GPIO pinned, quad-USB ported, credit card sized bomb of DIY joy. And while you can use most of our great Model B accessories by hooking up our downgrade cable, its probably a good time to upgrade your set up and accessorize using all of the 40 pins. That's why we now carry the Assembled Adafruit Pi T-Cobbler Plus - Breakout + Cable for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
